// Logisim project E02.circ as structural Verilog
module mux_1bit (
  input  A,
  input  B,
  input  OP,
  output x
);

  wire and_1_out, and_2_out, not_1_out;

  not not_1 (not_1_out, OP);
  and and_1 (and_1_out, B, OP);
  and and_2 (and_2_out, A, not_1_out);
  or or_1 (x, and_1_out, and_2_out);
endmodule

module mux_2bits (
  input  A,
  input  O,
  input  N,
  input  SUM,
  input  S1,
  input  S0,
  output out_7
);

  wire and_1_out, and_2_out, and_3_out, and_5_out, not_1_out, not_2_out, not_3_out, not_4_out;

  not not_1 (not_1_out, S1);
  not not_2 (not_2_out, S0);
  not not_3 (not_3_out, S1);
  not not_4 (not_4_out, S0);
  and and_1 (and_1_out, A, not_1_out, not_2_out);
  and and_2 (and_2_out, O, not_3_out, S0);
  and and_3 (and_3_out, N, S1, not_4_out);
  // AND_Gate and_4 is placed but not wired
  and and_5 (and_5_out, SUM, S1, S0);
  // AND_Gate and_6 is placed but not wired
  or or_1 (out_7, and_1_out, and_2_out, and_3_out, and_5_out);
endmodule

module Somador (
  input  Ci,
  input  X,
  input  Y,
  output R,
  output Co
);

  wire and_1_out, and_2_out, xor_1_out;

  xor xor_1 (xor_1_out, X, Y);
  and and_1 (and_1_out, Y, X);
  and and_2 (and_2_out, Ci, xor_1_out);
  xor xor_2 (R, Ci, xor_1_out);
  or or_1 (Co, and_2_out, and_1_out);
endmodule

module ula_4bits (
  input  S1,
  input  S0,
  input  Bin,
  input  B3,
  input  B2,
  input  B1,
  input  B0,
  input  A3,
  input  A2,
  input  A1,
  input  A0,
  output out_12,
  output out_13,
  output out_14,
  output out_15,
  output Co
);

  wire ula_1bit_1_co, ula_1bit_2_co, ula_1bit_3_co;

  ula_1bit ula_1bit_1 (.A(A0), .B(B0), .S1(S1), .S0(S0), .Binvert(Bin), .Ci(Bin), .out_7(out_12), .Co(ula_1bit_1_co));
  ula_1bit ula_1bit_2 (
    .A(A1), .B(B1), .S1(S1), .S0(S0), .Binvert(Bin), .Ci(ula_1bit_1_co), .out_7(out_13), .Co(ula_1bit_2_co));
  ula_1bit ula_1bit_3 (
    .A(A2), .B(B2), .S1(S1), .S0(S0), .Binvert(Bin), .Ci(ula_1bit_2_co), .out_7(out_14), .Co(ula_1bit_3_co));
  ula_1bit ula_1bit_4 (.A(A3), .B(B3), .S1(S1), .S0(S0), .Binvert(Bin), .Ci(ula_1bit_3_co), .out_7(out_15), .Co(Co));
endmodule

module ula_1bit (
  input  A,
  input  B,
  input  S1,
  input  S0,
  input  Binvert,
  input  Ci,
  output out_7,
  output Co
);

  wire and_1_out, mux_1bit_1_x, not_1_out, not_2_out, or_1_out, somador_1_r;

  not not_1 (not_1_out, B);
  mux_1bit mux_1bit_1 (.A(B), .B(not_1_out), .OP(Binvert), .x(mux_1bit_1_x));
  and and_1 (and_1_out, A, mux_1bit_1_x);
  or or_1 (or_1_out, A, mux_1bit_1_x);
  not not_2 (not_2_out, A);
  Somador somador_1 (.Ci(Ci), .X(A), .Y(mux_1bit_1_x), .R(somador_1_r), .Co(Co));
  mux_2bits mux_2bits_1 (
    .A(and_1_out), .O(or_1_out), .N(not_2_out), .SUM(somador_1_r), .S1(S1), .S0(S0), .out_7(out_7));
endmodule
