// Logisim project E02_pt2.circ as structural Verilog: 2 circuits, main circuit main
module main (
  input  b,
  input  a
);

  Multiplexer multiplexer_1 ();  // open: in0, in1, out, sel
endmodule

module E02 (
  input  [3:0] a,
  input  [3:0] b,
  input  [3:0] s,
  output [3:0] f
);

  wire [3:0] and_1_out, and_2_out, and_3_out, nand_1_out, nor_1_out, not_1_out, not_2_out, not_3_out,
       not_4_out, not_5_out, not_6_out, not_7_out, or_1_out, or_2_out, or_3_out, xor_1_out, xor_2_out;

  assign not_1_out = ~a;  // NOT_Gate not_1, 4 bits wide
  assign nor_1_out = ~(a | b);  // NOR_Gate nor_1, 4 bits wide
  assign not_2_out = ~a;  // NOT_Gate not_2, 4 bits wide
  assign and_1_out = not_2_out & b;  // AND_Gate and_1, 4 bits wide
  assign not_3_out = ~b;  // NOT_Gate not_3, 4 bits wide
  assign and_2_out = a & not_4_out;  // AND_Gate and_2, 4 bits wide
  assign not_4_out = ~b;  // NOT_Gate not_4, 4 bits wide
  assign not_5_out = ~a;  // NOT_Gate not_5, 4 bits wide
  assign or_1_out = not_5_out | b;  // OR_Gate or_1, 4 bits wide
  assign and_3_out = a & b;  // AND_Gate and_3, 4 bits wide
  assign or_2_out = a | not_6_out;  // OR_Gate or_2, 4 bits wide
  assign not_6_out = ~b;  // NOT_Gate not_6, 4 bits wide
  assign or_3_out = a | b;  // OR_Gate or_3, 4 bits wide
  assign nand_1_out = ~(a & b);  // NAND_Gate nand_1, 4 bits wide
  assign xor_1_out = a ^ b;  // XOR_Gate xor_1, 4 bits wide
  assign xor_2_out = a ^ b;  // XOR_Gate xor_2, 4 bits wide
  assign not_7_out = ~xor_2_out;  // NOT_Gate not_7, 4 bits wide
  Multiplexer #(.select(4), .width(4)) multiplexer_1 (
    .in0(not_1_out), .in1(nor_1_out), .in2(and_1_out), .in3(4'b0000), .in4(nand_1_out), .in5(not_3_out),
    .in6(xor_1_out), .in7(and_2_out), .in8(or_1_out), .in9(not_7_out), .in10(b), .in11(and_3_out),
    .in12(4'b1111), .in13(or_2_out), .in14(or_3_out), .in15(a), .out(f), .sel(s));
endmodule
